# Fritzing sketch receiver (saved by Fritzing 0.9.2b)
breadboards: 1

parts:
  Receiver = Arduino Uno (Rev3)
  R1 = Resistor [tolerance=±5% resistance=10k package=THT]
  R2 = Photocell (LDR) [package=THT]

nets:
  N1: Receiver.GND, R1.Pin_0
  N2: Receiver.D0/RX, R1.Pin_1, R2.pin_0
  N3: Receiver.5V, R2.pin_1
