# Fritzing sketch sender (saved by Fritzing 0.9.2b)
breadboards: 1

parts:
  Sender = Arduino Uno (Rev3)
  R1 = Resistor [tolerance=±5% resistance=100 package=THT]
  LED1 = LED - 5mm [color="White (8000K)" package="5 mm [THT]"]

nets:
  N1: Sender.GND, R1.Pin_0
  N2: Sender.D1/TX, LED1.anode
  N3: R1.Pin_1, LED1.cathode
